// Logisim project tipoR_tipoI.circ as structural Verilog: 1 circuit, main circuit main
module main (
  input  [19:0] ENDERECO,
  input  REG_DEST,
  input  [31:0] DADO,
  input  [3:0] ALU_OP,
  input  STORE,
  input  REG_W,
  input  ALU_SRC,
  input  LOAD,
  input  RESET,
  output [31:0] DADO_2
);

  wire clock_1_out, CLOCK_2_out, clock_3_out, registerfile_1_p1, registerfile_1_p7;
  wire [4:0] multiplexer_1_out;
  wire [31:0] adder_1_out, bit_extender_1_out, mips_alu_1_p2, mipsprogramrom_1_p2, register_1_q,
       registerfile_1_p8;

  Adder #(.width(32)) adder_1 (.a(register_1_q), .b(32'h4), .out(adder_1_out));  // open: cin, cout
  Clock clock_1 (.out(clock_1_out));
  Register #(.width(32)) register_1 (.D(adder_1_out), .Q(register_1_q), .clk(clock_1_out));  // open: en, clr
  // MIPSProgramROM mipsprogramrom_1: pin names not known; wires that end beside it: register_1_q, mipsprogramrom_1_p2
  Multiplexer #(.width(5), .enable("false")) multiplexer_1 (
    .in0(mipsprogramrom_1_p2[15:11]), .in1(mipsprogramrom_1_p2[20:16]), .out(multiplexer_1_out),
    .sel(REG_DEST));
  Clock CLOCK_2 (.out(CLOCK_2_out));
  // RegisterFile registerfile_1: pin names not known; wires that end beside it: registerfile_1_p1, CLOCK_2_out, REG_W, multiplexer_1_out, mipsprogramrom_1_p2[25:21], mipsprogramrom_1_p2[20:16], registerfile_1_p7, registerfile_1_p8
  assign bit_extender_1_out = {{16{1'b0}}, mipsprogramrom_1_p2[15:0]};  // Bit_Extender bit_extender_1
  // Mips_ALU mips_alu_1: pin names not known; wires that end beside it: registerfile_1_p7, mips_alu_1_p2, ALU_OP, registerfile_1_p1
  Multiplexer #(.width(32), .enable("false")) multiplexer_2 (
    .in0(registerfile_1_p8), .in1(bit_extender_1_out), .out(mips_alu_1_p2), .sel(ALU_SRC));
  Clock clock_3 (.out(clock_3_out));
  // MIPS_RAM mips_ram_1: pin names not known; wires that end beside it: ENDERECO, DADO, STORE, clock_3_out, LOAD, RESET, DADO_2

  // Notes on the sheet:
  //   tipo R
  //   tipo I
  //   (controle)
  //   DADO
  //   (controle)
  //   END
  //   END
  //   END
  //   DESTINO
  //   ORIGEM 2
  //   ORIGEM 1
  //   DADO
  //   tipo R
  //   tipo I
  //   (controle)
  //   SOMA
endmodule
